# Fritzing sketch Untitled Sketch (saved by Fritzing 0.9.3b)

parts:
  Часть1 = Arduino Nano (Rev3.0)
  J1 = Basic Servo
  R1 = Resistor [tolerance=±5% resistance=220 package=THT]
  R2 = Resistor [tolerance=±5% resistance=220 package=THT]

nets:
  GND: Часть1.GND, J1.gnd, R2.Pin_0
  N1: Часть1.D2, R1.Pin_0, R2.Pin_1
  N2: Часть1.D5, J1.pulse

notes:
  Источник питания 5 вольт
  - +
  Датчик
  7кОм
  5кОм
