# Fritzing sketch Схема сборки (saved by Fritzing 0.9.3b)

parts:
  Pololu_A1 = Pololu A4988 [package=SO16]
  M1 = Stepper Motor - Bipolar
  Часть1 = Arduino Nano (Rev3.0)
  Power_plug1 = Power plug
  C1 = Electrolytic Capacitor [capacitance=1µF package="100 mil [THT, electrolytic]"]
  R2 = Resistor [tolerance=±5% resistance=220 package=THT]
  R3 = Resistor [tolerance=±5% resistance=220 package=THT]

nets:
  N1: Pololu_A1.RESET, Pololu_A1.SLEEP
  N2: Pololu_A1.STEP, Часть1.D6
  N3: Pololu_A1.DIR, Часть1.D8
  N4: Pololu_A1.GND#8, Часть1.GND
  VDD: Pololu_A1.VDD, Часть1.5V
  N5: Pololu_A1.1B, M1.D
  N6: Pololu_A1.1A, M1.B
  N7: Pololu_A1.2A, M1.C
  N8: Pololu_A1.2B, M1.A
  N9: Pololu_A1.GND#14, Power_plug1.GND, C1.+
  N10: Pololu_A1.VMOT, Power_plug1.VCC, C1.-
  N11: Часть1.D2, R2.Pin_1, R3.Pin_1

notes:
  Электролетический конденсатор 470-5000 uF, с напряжением больше VCC
  Источник питания 5 вольт
  - +
  Датчик
  7кОм
  5кОм
  Питание 8-35 v
  GND
  VCC
  1B
  1A
  2A
  2B
  STEP
  DIR
