# Fritzing sketch scheme (saved by Fritzing 0.9.3b)

parts:
  Часть1 = Adafruit TCA9548A
  Часть3 = Arduino Nano (Rev3.0)
  VCC1 = 4 x AAA Battery Mount
  M1 = HTU21d
  M2 = HTU21d
  M3 = HTU21d

nets:
  N1: Часть1.6SDA, M3.SDA
  N2: Часть1.6SCL, M3.SCL
  N3: Часть1.7SDA, M2.SDA
  N4: Часть1.7SCL, M2.SCL
  VIN: Часть1.VCC, Часть3.VIN, VCC1.+, M1.VIN, M2.VIN
  GND: Часть1.GND, Часть3.GND, VCC1.-, M1.GND, M3.GND
  N5: Часть1.INPUTSDA, Часть3.A4
  N6: Часть1.INPUTSCL, Часть3.A5
  N7: Часть1.0SDA, M1.SDA
  N8: Часть1.0SCL, M1.SCL

notes:
  SC <--- SCL
  SD <--- SDA
  GND <--- GND
  VIN <--- VIN
  и так далее...

custom parts:
  Adafruit TCA9548A: You just found the perfect I2C sensor, and you want to wire up two or three or more of them to your Arduino when you realize "Uh oh, this chip has a fixed I2C address, and from what I know about I2C, you cannot have two devices with the same address on the same SDA/SCL pins!" Are you out of luck? You would be, if you didn't have this ultra-cool TCA9548A 1-to-8 I2C multiplexer! Finally, a way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
  4 x AAA Battery Mount: A 4 x AAA battery pack (4.8 Volts with recharables)
  HTU21d: Temperature Humidity Sensor, I2C
