# Fritzing sketch Заказ 17 (saved by Fritzing 0.9.3b)

parts:
  WeMos_D1_Mini1 = WeMos D1 Mini
  Часть1 = Arduino Uno (Rev3) - ICSP
  ds18b20_probe1 = ds18b20 probe
  Module1 = Relay
  ds18b20_probe2 = ds18b20 probe
  ds18b20_probe3 = ds18b20 probe
  Module2 = Relay
  Module3 = Relay
  Module4 = Relay
  Module5 = Relay
  Module6 = Relay
  Power_plug1 = Power plug
  ds18b20_probe4 = ds18b20 probe
  R1 = Resistor [tolerance=±5% resistance=4.7k package=THT]
  R2 = Resistor [tolerance=±5% resistance=4.7k package=THT]

nets:
  5V: WeMos_D1_Mini1.5V, Module1.power, Module2.power, Module3.power, Module4.power, Module5.power, Module6.power, Power_plug1.VCC
  N1: WeMos_D1_Mini1.D3, Часть1.D2
  GND: WeMos_D1_Mini1.G, Часть1.GND, ds18b20_probe1.pin3, Module1.ground, ds18b20_probe2.pin3, ds18b20_probe3.pin3, Module2.ground, Module3.ground, Module4.ground, Module5.ground, Module6.ground, Power_plug1.GND
  N2: WeMos_D1_Mini1.RST, Часть1.D8
  N3: Часть1.A0, ds18b20_probe1.pin2
  N4: Часть1.A2, ds18b20_probe2.pin2
  N5: Часть1.A4/SDA, ds18b20_probe3.pin2
  N6: Часть1.A5/SCL, ds18b20_probe4.pin2, R1.Pin_0
  N7: Часть1.D10_PWM/SS, Module5.signal
  N8: Часть1.D11_PWM/MOSI, Module2.signal
  N9: Часть1.D12/MISO, Module1.signal
  N10: Часть1.D5_PWM, Module6.signal
  N11: Часть1.D6_PWM, Module4.signal
  N12: Часть1.D7, Module3.signal
  N13: Часть1.VIN, ds18b20_probe1.pin1, ds18b20_probe2.pin1, ds18b20_probe3.pin1, ds18b20_probe4.pin1, R2.Pin_1
