# Fritzing sketch 28 (saved by Fritzing 0.9.5d)

parts:
  Компонент1 = Arduino Nano (Rev3.0)
  R1 = Resistor [tolerance=±5% resistance=220 package=THT]
  LED1 = LED - 5mm [color="Red (633nm)" package="5 mm [THT]"]
  S1 = Pushbutton [package="[THT]"]
  LED2 = LED - 5mm [color="Orange (605nm)" package="5 mm [THT]"]
  LED3 = LED - 5mm [color="Green (555nm)" package="5 mm [THT]"]
  IC1 = Voltage Regulator [package=sot23-5]
  Buzzer2 = Buzzer  # not connected

nets:
  N1: Компонент1.GND, R1.Pin_0, S1.Pin_3, S1.Pin_4, IC1.EN
  N2: Компонент1.D3, S1.Pin_1, S1.Pin_2
  N3: Компонент1.D5, LED1.anode
  N4: Компонент1.D7, LED2.anode
  N5: Компонент1.D9, LED3.anode
  N6: Компонент1.D11/MOSI, IC1.GND
  N7: Компонент1.5V, IC1.IN
  N8: R1.Pin_1, LED1.cathode
