# Fritzing sketch project32 (saved by Fritzing 0.9.5d)
breadboards: 2

parts:
  Компонент1 = Arduino Nano (Rev3.0) (ICSP)
  LED1 = smd LED [color="Red (633nm)" package="0805 [SMD]"]
  S1 = Pushbutton [package="[THT]"]
  LED6 = smd LED [color="Red (633nm)" package="0805 [SMD]"]
  LED7 = smd LED [color="Red (633nm)" package="0805 [SMD]"]
  LED8 = smd LED [color="Red (633nm)" package="0805 [SMD]"]
  LED9 = smd LED [color="Red (633nm)" package="0805 [SMD]"]
  LED10 = smd LED [color="Red (633nm)" package="0805 [SMD]"]
  LED11 = smd LED [color="Red (633nm)" package="0805 [SMD]"]
  LED12 = smd LED [color="Red (633nm)" package="0805 [SMD]"]
  LED13 = smd LED [color="Red (633nm)" package="0805 [SMD]"]
  LED14 = smd LED [color="Red (633nm)" package="0805 [SMD]"]
  LED15 = smd LED [color="Red (633nm)" package="0805 [SMD]"]
  LED16 = smd LED [color="Red (633nm)" package="0805 [SMD]"]
  R1 = Resistor [tolerance=±5% resistance=220 package=THT]
  S2 = Pushbutton [package="[THT]"]
  S3 = Pushbutton [package="[THT]"]
  S4 = Pushbutton [package="[THT]"]
  S5 = Pushbutton [package="[THT]"]
  S6 = Pushbutton [package="[THT]"]

nets:
  N1: Компонент1.GND, S1.Pin_1, S1.Pin_2, R1.Pin_0, S2.Pin_1, S2.Pin_2, S3.Pin_1, S3.Pin_2, S4.Pin_1, S4.Pin_2, S5.Pin_1, S5.Pin_2, S6.Pin_1, S6.Pin_2
  N2: Компонент1.D2, LED1.anode
  N3: Компонент1.D3, LED6.anode
  N4: Компонент1.D4, LED7.anode
  N5: Компонент1.D5, LED8.anode
  N6: Компонент1.D6, LED9.anode
  N7: Компонент1.D7, LED10.anode
  N8: Компонент1.D8, LED11.anode
  N9: Компонент1.D9, LED12.anode
  N10: Компонент1.D10, LED13.anode
  N11: Компонент1.D11/MOSI, LED14.anode
  N12: Компонент1.D12/MISO, LED15.anode
  N13: Компонент1.A5, S6.Pin_3, S6.Pin_4
  N14: Компонент1.A4, S5.Pin_3, S5.Pin_4
  N15: Компонент1.A3, S4.Pin_3, S4.Pin_4
  N16: Компонент1.A2, S3.Pin_3, S3.Pin_4
  N17: Компонент1.A1, S2.Pin_3, S2.Pin_4
  N18: Компонент1.A0, S1.Pin_3, S1.Pin_4
  N19: Компонент1.D13/SCK, LED16.anode
  N20: LED1.cathode, LED6.cathode, LED7.cathode, LED8.cathode, LED9.cathode, LED10.cathode, LED11.cathode, LED12.cathode, LED13.cathode, LED14.cathode, LED15.cathode, LED16.cathode, R1.Pin_1
