# Fritzing sketch project37 sketch (saved by Fritzing 0.9.5d)

parts:
  Компонент1 = Arduino Uno (Rev3)
  LED1 = LED - 5mm [color="Red (633nm)" package="5 mm [THT]"]
  Mosfet_Module1 = Mosfet Module
  Компонент2 = LCD1602-I2C
  Компонент3 = BH1750
  VCC1 = Battery block 9V

nets:
  N1: Компонент1.A4/SDA, Компонент2.SDA, Компонент3.SDA
  N2: Компонент1.A5/SCL, Компонент2.SCL, Компонент3.SCL
  GND: Компонент1.GND, Mosfet_Module1.GND, Mosfet_Module1.IN-, Компонент2.GND, Компонент3.GND, VCC1.-
  N3: Компонент1.D5_PWM, Mosfet_Module1.SIG
  VCC: Компонент1.5V, Компонент2.VCC, Компонент3.VCC
  N4: Компонент1.VIN, Mosfet_Module1.IN+, VCC1.+
  N5: LED1.cathode, Mosfet_Module1.OUT-
  N6: LED1.anode, Mosfet_Module1.OUT+

custom parts:
  LCD1602-I2C: A standard character display, usually with 2x16 characters. Comes in many colors with LCM1602 IIC attached.
  BH1750: Light Sensor
